// Logisim project ben_eater_602_logism.circ as structural Verilog: 1 circuit, main circuit main
module main (
  input  in_1,
  output w0r1,
  output [15:0] ADDR,
  output [7:0] DATA
);

  wire reset_out, w65c02s_pdip_40_1_p18, w65c02s_pdip_40_1_p20;
  wire [7:0] w65c22_1_p7, w65c22_1_p9;

  ROM #(.addrWidth(16)) rom_1 (.addr(ADDR), .data(DATA));
  // W65C02S__PDIP_40 w65c02s_pdip_40_1: pin names not known; wires that end beside it: ADDR, 1'b1, 1'b1, 1'b1, 1'b1, ADDR[0], ADDR[1], ADDR[2], ADDR[3], ADDR[4], ADDR[5], ADDR[6], ADDR[7], ADDR[8], ADDR[9], ADDR[10], ADDR[11], w65c02s_pdip_40_1_p18, 1'b1, w65c02s_pdip_40_1_p20, 1'b1, w0r1, DATA[0], DATA[1], DATA[2], DATA[3], DATA[4], DATA[5], DATA[6], DATA[7], ADDR[15], ADDR[14], ADDR[13], ADDR[12], 1'b0
  Clock #(.highDuration(2), .lowDuration(2)) clock_1 (.out(w65c02s_pdip_40_1_p20));
  Pull_Resistor #(.pull(1)) pull_resistor_1 (.node(w65c02s_pdip_40_1_p18));
  Button reset (.out(reset_out));
  not not_1 (w65c02s_pdip_40_1_p18, reset_out);
  // W65C22 w65c22_1: pin names not known; wires that end beside it: ADDR[3:0], DATA, w65c02s_pdip_40_1_p20, 1'b1, in_1, w0r1, w65c22_1_p7, DATA, w65c22_1_p9
  LedBar ledbar_1 (
    .led0(w65c22_1_p7[7]), .led1(w65c22_1_p7[6]), .led2(w65c22_1_p7[5]), .led3(w65c22_1_p7[4]),
    .led4(w65c22_1_p7[3]), .led5(w65c22_1_p7[2]), .led6(w65c22_1_p7[1]), .led7(w65c22_1_p7[0]));
  LedBar ledbar_2 (
    .led0(w65c22_1_p9[7]), .led1(w65c22_1_p9[6]), .led2(w65c22_1_p9[5]), .led3(w65c22_1_p9[4]),
    .led4(w65c22_1_p9[3]), .led5(w65c22_1_p9[2]), .led6(w65c22_1_p9[1]), .led7(w65c22_1_p9[0]));

  // Notes on the sheet:
  //   contents of rom_1 (hex, n*v repeats v):
  //   a9 42 8d 0 60 65527*ea 0 0 ea ea
endmodule
